// Logisim project aiAlu.circ as structural Verilog: 24 circuits, main circuit Half Adder
module Half_Adder (
  input  a,
  input  b,
  output S,
  output c
);

  xor xor_1 (S, a, b);
  and and_1 (c, a, b);
endmodule

module Full_Adder (
  input  C0,
  input  a,
  input  b,
  output S,
  output c
);

  wire and_1_out, and_2_out, and_3_out, xor_1_out;

  xor xor_1 (xor_1_out, a, b);
  and and_1 (and_1_out, C0, a);
  and and_2 (and_2_out, C0, b);
  and and_3 (and_3_out, a, b);
  xor xor_2 (S, xor_1_out, C0);
  or or_1 (c, and_1_out, and_2_out, and_3_out);
endmodule

module Circuito_4_Bit (
  input  a3,
  input  a2,
  input  a1,
  input  a0,
  input  b3,
  input  b2,
  input  b1,
  input  b0,
  output cout,
  output s3,
  output s2,
  output s1,
  output s0
);

  wire full_adder_2_c, full_adder_3_c, half_adder_1_c;

  Full_Adder full_adder_1 (.S(s3), .c(cout), .C0(full_adder_2_c), .a(a3), .b(b3));
  Full_Adder full_adder_2 (.S(s2), .c(full_adder_2_c), .C0(full_adder_3_c), .a(a2), .b(b2));
  Full_Adder full_adder_3 (.S(s1), .c(full_adder_3_c), .C0(half_adder_1_c), .a(a1), .b(b1));
  Half_Adder half_adder_1 (.S(s0), .c(half_adder_1_c), .a(b0), .b(a0));
endmodule

module sommatore_4_bit (
  input  in_1,
  input  in_2,
  input  in_3,
  input  in_4,
  input  in_5,
  input  in_6,
  input  in_7,
  input  in_8,
  output out_9,
  output out_10,
  output out_11,
  output out_12,
  output out_13
);

  Circuito_4_Bit circuito_4_bit_1 (
    .a3(in_1), .a2(in_2), .a1(in_3), .a0(in_4), .b3(in_5), .b2(in_6), .b1(in_7), .b0(in_8), .cout(out_9),
    .s3(out_10), .s2(out_11), .s1(out_12), .s0(out_13));
endmodule

module circuito_8_bit (
  input  cin,
  input  a3,
  input  a2,
  input  a1,
  input  a0,
  input  b3,
  input  b2,
  input  b1,
  input  b0,
  output out_10,
  output out_11,
  output out_12,
  output out_13,
  output out_14
);

  wire full_adder_2_c, full_adder_3_c, full_adder_4_c;

  Full_Adder full_adder_1 (.S(out_11), .c(out_10), .C0(full_adder_2_c), .a(a3), .b(b3));
  Full_Adder full_adder_2 (.S(out_12), .c(full_adder_2_c), .C0(full_adder_3_c), .a(a2), .b(b2));
  Full_Adder full_adder_3 (.S(out_13), .c(full_adder_3_c), .C0(full_adder_4_c), .a(a1), .b(b1));
  Full_Adder full_adder_4 (.S(out_14), .c(full_adder_4_c), .C0(cin), .a(a0), .b(b0));
endmodule

module sommatore_8_bit (
  input  in_1,
  input  in_2,
  input  in_3,
  input  in_4,
  input  in_5,
  input  in_6,
  input  in_7,
  input  in_8,
  input  in_9,
  input  in_10,
  input  in_11,
  input  in_12,
  input  in_13,
  input  in_14,
  input  in_15,
  input  in_16,
  output out_17,
  output out_18,
  output out_19,
  output out_20,
  output out_21,
  output out_22,
  output out_23,
  output out_24,
  output out_25
);

  wire circuito_4_bit_1_cout;

  LED led_1 (.in(out_17));
  circuito_8_bit circuito_8_bit_1 (
    .a3(in_9), .a2(in_10), .a1(in_11), .a0(in_12), .b3(in_13), .b2(in_14), .b1(in_15), .b0(in_16),
    .cin(circuito_4_bit_1_cout), .out_10(out_17), .out_11(out_18), .out_12(out_19), .out_13(out_20),
    .out_14(out_21));
  Circuito_4_Bit circuito_4_bit_1 (
    .a3(in_1), .a2(in_2), .a1(in_3), .a0(in_4), .b3(in_5), .b2(in_6), .b1(in_7), .b0(in_8),
    .cout(circuito_4_bit_1_cout), .s3(out_22), .s2(out_23), .s1(out_24), .s0(out_25));
endmodule

module Sommatore_8_bit (
  input  [7:0] in_1,
  input  [7:0] in_2,
  output out_3,
  output [7:0] out_4
);

  sommatore_8_bit sommatore_8_bit_1 (
    .in_9(in_1[7]), .in_10(in_1[6]), .in_11(in_1[5]), .in_12(in_1[4]), .in_13(in_2[7]), .in_14(in_2[6]),
    .in_15(in_2[5]), .in_16(in_2[4]), .in_1(in_1[3]), .in_2(in_1[2]), .in_3(in_1[1]), .in_4(in_1[0]),
    .in_5(in_2[3]), .in_6(in_2[2]), .in_7(in_2[1]), .in_8(in_2[0]), .out_18(out_4[7]), .out_19(out_4[6]),
    .out_20(out_4[5]), .out_21(out_4[4]), .out_22(out_4[3]), .out_23(out_4[2]), .out_24(out_4[1]),
    .out_25(out_4[0]), .out_17(out_3));
endmodule

module compl__a_2 (
  input  [7:0] in_1,
  output [7:0] out_2,
  output out_3
);

  wire half_adder_1_c, half_adder_2_c, half_adder_3_c, half_adder_4_c, half_adder_5_c, half_adder_6_c,
       half_adder_7_c;
  wire [7:0] not_1_out;

  assign not_1_out = ~in_1;  // NOT_Gate not_1, 8 bits wide
  Half_Adder half_adder_1 (.S(out_2[0]), .c(half_adder_1_c), .a(1'b1), .b(not_1_out[0]));
  Half_Adder half_adder_2 (.S(out_2[1]), .c(half_adder_2_c), .a(half_adder_1_c), .b(not_1_out[1]));
  Half_Adder half_adder_3 (.S(out_2[2]), .c(half_adder_3_c), .a(half_adder_2_c), .b(not_1_out[2]));
  Half_Adder half_adder_4 (.S(out_2[3]), .c(half_adder_4_c), .a(half_adder_3_c), .b(not_1_out[3]));
  Half_Adder half_adder_5 (.S(out_2[4]), .c(half_adder_5_c), .a(half_adder_4_c), .b(not_1_out[4]));
  Half_Adder half_adder_6 (.S(out_2[5]), .c(half_adder_6_c), .a(half_adder_5_c), .b(not_1_out[5]));
  Half_Adder half_adder_7 (.S(out_2[6]), .c(half_adder_7_c), .a(half_adder_6_c), .b(not_1_out[6]));
  Half_Adder half_adder_8 (.S(out_2[7]), .c(out_3), .a(half_adder_7_c), .b(not_1_out[7]));
  LED led_1 (.in(out_3));
endmodule

module sottrattore_8_bit (
  input  [7:0] in_1,
  input  [7:0] in_2,
  output out_3,
  output [7:0] out_4
);

  wire compl_a_2_1_out_3;
  wire [7:0] compl_a_2_1_out_2;

  // Probe on in_1
  // Probe on in_2
  LED led_1 (.in(compl_a_2_1_out_3));
  compl__a_2 compl_a_2_1 (.in_1(in_2), .out_2(compl_a_2_1_out_2), .out_3(compl_a_2_1_out_3));
  sommatore_8_bit sommatore_8_bit_1 (
    .in_9(in_1[7]), .in_10(in_1[6]), .in_11(in_1[5]), .in_12(in_1[4]), .in_13(compl_a_2_1_out_2[7]),
    .in_14(compl_a_2_1_out_2[6]), .in_15(compl_a_2_1_out_2[5]), .in_16(compl_a_2_1_out_2[4]), .in_1(in_1[3]),
    .in_2(in_1[2]), .in_3(in_1[1]), .in_4(in_1[0]), .in_5(compl_a_2_1_out_2[3]), .in_6(compl_a_2_1_out_2[2]),
    .in_7(compl_a_2_1_out_2[1]), .in_8(compl_a_2_1_out_2[0]), .out_18(out_4[7]), .out_19(out_4[6]),
    .out_20(out_4[5]), .out_21(out_4[4]), .out_22(out_4[3]), .out_23(out_4[2]), .out_24(out_4[1]),
    .out_25(out_4[0]), .out_17(out_3));
  // Probe on out_4
endmodule

module mux (
  input  d1,
  input  d0,
  input  s0,
  output out_4
);

  wire and_1_out, and_2_out, not_1_out;

  not not_1 (not_1_out, s0);
  and and_1 (and_1_out, d0, not_1_out);
  and and_2 (and_2_out, d1, s0);
  or or_1 (out_4, and_1_out, and_2_out);
endmodule

module mux_compatto (
  input  in_1,
  input  [7:0] in_2,
  input  [7:0] in_3,
  output [7:0] out_4
);

  // Probe on in_3
  // Probe on in_2
  mux_2_a_1 mux_2_a_1_1 (
    .in_3(in_1), .out_18(out_4[7]), .out_19(out_4[6]), .out_20(out_4[5]), .out_21(out_4[4]),
    .out_22(out_4[3]), .out_23(out_4[2]), .out_24(out_4[1]), .out_25(out_4[0]), .in_1(in_3[7]),
    .in_6(in_3[5]), .in_10(in_3[3]), .in_14(in_3[1]), .in_2(in_2[7]), .in_7(in_2[5]), .in_11(in_2[3]),
    .in_15(in_2[1]), .in_8(in_3[4]), .in_12(in_3[2]), .in_16(in_3[0]), .in_4(in_3[6]), .in_9(in_2[4]),
    .in_13(in_2[2]), .in_17(in_2[0]), .in_5(in_2[6]));
  // Probe on out_4
endmodule

module mux_2_a_1 (
  input  in_1,
  input  in_2,
  input  in_3,
  input  in_4,
  input  in_5,
  input  in_6,
  input  in_7,
  input  in_8,
  input  in_9,
  input  in_10,
  input  in_11,
  input  in_12,
  input  in_13,
  input  in_14,
  input  in_15,
  input  in_16,
  input  in_17,
  output out_18,
  output out_19,
  output out_20,
  output out_21,
  output out_22,
  output out_23,
  output out_24,
  output out_25
);

  mux mux_1 (.out_4(out_18), .d1(in_1), .d0(in_2), .s0(in_3));
  mux mux_2 (.out_4(out_20), .d1(in_6), .d0(in_7), .s0(in_3));
  mux mux_3 (.out_4(out_22), .d1(in_10), .d0(in_11), .s0(in_3));
  mux mux_4 (.out_4(out_24), .d1(in_14), .d0(in_15), .s0(in_3));
  mux mux_5 (.out_4(out_19), .d1(in_4), .d0(in_5), .s0(in_3));
  mux mux_6 (.out_4(out_21), .d1(in_8), .d0(in_9), .s0(in_3));
  mux mux_7 (.out_4(out_23), .d1(in_12), .d0(in_13), .s0(in_3));
  mux mux_8 (.out_4(out_25), .d1(in_16), .d0(in_17), .s0(in_3));
endmodule

module somma_e_sottrazione (
  input  [7:0] in_1,
  input  [7:0] in_2,
  input  in_3,
  output out_4,
  output [7:0] out_5,
  output out_6
);

  wire [7:0] sommatore_8_bit_1_out_4, sottrattore_8_bit_1_out_4;

  // Probe on in_1
  // Probe on in_2
  Sommatore_8_bit sommatore_8_bit_1 (.in_1(in_1), .in_2(in_2), .out_3(out_4), .out_4(sommatore_8_bit_1_out_4));
  sottrattore_8_bit sottrattore_8_bit_1 (.in_1(in_1), .in_2(in_2), .out_3(out_6), .out_4(sottrattore_8_bit_1_out_4));
  // Probe on sommatore_8_bit_1_out_4
  // Probe on sottrattore_8_bit_1_out_4
  // Probe on out_5
  mux_compatto mux_compatto_1 (
    .in_2(sommatore_8_bit_1_out_4), .in_3(sottrattore_8_bit_1_out_4), .out_4(out_5), .in_1(in_3));

  // Other names for the same wires on the sheet: A[7:0] = in_1; B[7:0] = in_2
endmodule

module arit (
  input  selezione,
  input  [7:0] A,
  input  [7:0] B,
  output [7:0] risultato,
  output overflow,
  output carry
);

  // Probe on A
  // Probe on B
  somma_e_sottrazione somma_e_sottrazione_1 (
    .out_4(overflow), .out_5(risultato), .out_6(carry), .in_1(A), .in_2(B), .in_3(selezione));
  // Probe on risultato
endmodule

module And_8_bit (
  input  [7:0] in_1,
  input  [7:0] in_2,
  output [7:0] out_3
);

  and and_1 (out_3[0], in_1[0], in_2[0]);
  and and_2 (out_3[1], in_1[1], in_2[1]);
  and and_3 (out_3[2], in_1[2], in_2[2]);
  and and_4 (out_3[3], in_1[3], in_2[3]);
  and and_5 (out_3[4], in_1[4], in_2[4]);
  and and_6 (out_3[5], in_1[5], in_2[5]);
  and and_7 (out_3[6], in_2[6], in_1[6]);
  and and_8 (out_3[7], in_1[7], in_2[7]);
endmodule

module Or_8_bit (
  input  [7:0] in_1,
  input  [7:0] in_2,
  output [7:0] out_3
);

  or or_1 (out_3[0], in_1[0], in_2[0]);
  or or_2 (out_3[1], in_1[1], in_2[1]);
  or or_3 (out_3[2], in_1[2], in_2[2]);
  or or_4 (out_3[3], in_1[3], in_2[3]);
  or or_5 (out_3[4], in_1[4], in_2[4]);
  or or_6 (out_3[5], in_1[5], in_2[5]);
  or or_7 (out_3[6], in_2[6], in_1[6]);
  or or_8 (out_3[7], in_1[7], in_2[7]);
endmodule

module Ex_or_8bit (
  input  [7:0] in_1,
  input  [7:0] in_2,
  output [7:0] out_3
);

  xor xor_1 (out_3[0], in_1[0], in_2[0]);
  xor xor_2 (out_3[1], in_1[1], in_2[1]);
  xor xor_3 (out_3[2], in_1[2], in_2[2]);
  xor xor_4 (out_3[3], in_1[3], in_2[3]);
  xor xor_5 (out_3[4], in_1[4], in_2[4]);
  xor xor_6 (out_3[5], in_1[5], in_2[5]);
  xor xor_7 (out_3[6], in_2[6], in_1[6]);
  xor xor_8 (out_3[7], in_1[7], in_2[7]);
endmodule

module A_negato (
  input  [7:0] in_1,
  output [7:0] out_2
);

  not not_1 (out_2[0], in_1[0]);
  not not_2 (out_2[1], in_1[1]);
  not not_3 (out_2[2], in_1[2]);
  not not_4 (out_2[3], in_1[3]);
  not not_5 (out_2[4], in_1[4]);
  not not_6 (out_2[5], in_1[5]);
  not not_7 (out_2[6], in_1[6]);
  not not_8 (out_2[7], in_1[7]);
endmodule

module b_negato (
  input  [7:0] in_1,
  output [7:0] out_2
);

  not not_1 (out_2[0], in_1[0]);
  not not_2 (out_2[1], in_1[1]);
  not not_3 (out_2[2], in_1[2]);
  not not_4 (out_2[3], in_1[3]);
  not not_5 (out_2[4], in_1[4]);
  not not_6 (out_2[5], in_1[5]);
  not not_7 (out_2[6], in_1[6]);
  not not_8 (out_2[7], in_1[7]);
endmodule

module Mux_4_a_1 (
  input  in_1,
  input  in_2,
  input  in_3,
  input  in_4,
  input  in_5,
  input  in_6,
  output out_7
);

  wire and_1_out, and_2_out, and_3_out, and_4_out, not_1_out, not_2_out;

  not not_1 (not_1_out, in_6);
  not not_2 (not_2_out, in_5);
  and and_1 (and_1_out, not_2_out, in_1, not_1_out);
  and and_2 (and_2_out, not_2_out, in_6, in_2);
  and and_3 (and_3_out, in_5, not_1_out, in_3);
  and and_4 (and_4_out, in_5, in_4, in_6);
  or or_1 (out_7, and_1_out, and_2_out, and_3_out, and_4_out);
endmodule

module Mux_sjdiopna (
  input  in_1,
  input  in_2,
  input  in_3,
  input  in_4,
  input  in_5,
  input  in_6,
  input  in_7,
  input  in_8,
  input  in_9,
  input  in_10,
  input  in_11,
  output out_12
);

  wire mux_4_a_1_1_out_7, mux_4_a_1_2_out_7;

  Mux_4_a_1 mux_4_a_1_1 (
    .in_1(in_4), .in_2(in_5), .in_3(in_6), .in_4(in_7), .out_7(mux_4_a_1_1_out_7), .in_5(in_2), .in_6(in_3));
  Mux_4_a_1 mux_4_a_1_2 (
    .in_1(in_8), .in_2(in_9), .in_3(in_10), .in_4(in_11), .out_7(mux_4_a_1_2_out_7), .in_5(in_2), .in_6(in_3));
  mux mux_1 (.out_4(out_12), .d1(mux_4_a_1_2_out_7), .d0(mux_4_a_1_1_out_7), .s0(in_1));
endmodule

module _8_a_1 (
  input  in_1,
  input  in_2,
  input  in_3,
  input  in_4,
  input  in_5,
  input  in_6,
  input  in_7,
  input  in_8,
  input  in_9,
  input  in_10,
  input  in_11,
  input  in_12,
  input  in_13,
  input  in_14,
  input  in_15,
  input  in_16,
  input  in_17,
  input  in_18,
  input  in_19,
  input  in_20,
  input  in_21,
  input  in_22,
  input  in_23,
  input  in_24,
  input  in_25,
  input  in_26,
  input  in_27,
  input  in_28,
  input  in_29,
  input  in_30,
  input  in_31,
  input  in_32,
  input  in_33,
  input  in_34,
  input  in_35,
  input  in_36,
  input  in_37,
  input  in_38,
  input  in_39,
  input  in_40,
  input  in_41,
  input  in_42,
  input  in_43,
  input  in_44,
  input  in_45,
  input  in_46,
  input  in_47,
  input  in_48,
  input  in_49,
  input  in_50,
  input  in_51,
  input  in_52,
  input  in_53,
  input  in_54,
  input  in_55,
  input  in_56,
  input  in_57,
  input  in_58,
  input  in_59,
  input  in_60,
  input  in_61,
  input  in_62,
  input  in_63,
  input  in_64,
  input  in_65,
  input  in_66,
  input  in_67,
  output out_68,
  output out_69,
  output out_70,
  output out_71,
  output out_72,
  output out_73,
  output out_74,
  output out_75
);

  Mux_sjdiopna mux_sjdiopna_1 (
    .in_4(in_4), .in_5(in_8), .in_6(in_12), .in_7(in_16), .in_8(in_20), .in_9(in_24), .in_10(in_28),
    .in_11(in_32), .out_12(out_68), .in_1(in_1), .in_2(in_2), .in_3(in_3));
  Mux_sjdiopna mux_sjdiopna_2 (
    .in_4(in_36), .in_5(in_40), .in_6(in_44), .in_7(in_48), .in_8(in_52), .in_9(in_56), .in_10(in_60),
    .in_11(in_64), .out_12(out_72), .in_1(in_1), .in_2(in_2), .in_3(in_3));
  Mux_sjdiopna mux_sjdiopna_3 (
    .in_4(in_5), .in_5(in_9), .in_6(in_13), .in_7(in_17), .in_8(in_21), .in_9(in_25), .in_10(in_29),
    .in_11(in_33), .out_12(out_69), .in_1(in_1), .in_2(in_2), .in_3(in_3));
  Mux_sjdiopna mux_sjdiopna_4 (
    .in_4(in_37), .in_5(in_41), .in_6(in_45), .in_7(in_49), .in_8(in_53), .in_9(in_57), .in_10(in_61),
    .in_11(in_65), .out_12(out_73), .in_1(in_1), .in_2(in_2), .in_3(in_3));
  Mux_sjdiopna mux_sjdiopna_5 (
    .in_4(in_6), .in_5(in_10), .in_6(in_14), .in_7(in_18), .in_8(in_22), .in_9(in_26), .in_10(in_30),
    .in_11(in_34), .out_12(out_70), .in_1(in_1), .in_2(in_2), .in_3(in_3));
  Mux_sjdiopna mux_sjdiopna_6 (
    .in_4(in_38), .in_5(in_42), .in_6(in_46), .in_7(in_50), .in_8(in_54), .in_9(in_58), .in_10(in_62),
    .in_11(in_66), .out_12(out_74), .in_1(in_1), .in_2(in_2), .in_3(in_3));
  Mux_sjdiopna mux_sjdiopna_7 (
    .in_4(in_7), .in_5(in_11), .in_6(in_15), .in_7(in_19), .in_8(in_23), .in_9(in_27), .in_10(in_31),
    .in_11(in_35), .out_12(out_71), .in_1(in_1), .in_2(in_2), .in_3(in_3));
  Mux_sjdiopna mux_sjdiopna_8 (
    .in_4(in_39), .in_5(in_43), .in_6(in_47), .in_7(in_51), .in_8(in_55), .in_9(in_59), .in_10(in_63),
    .in_11(in_67), .out_12(out_75), .in_1(in_1), .in_2(in_2), .in_3(in_3));

  // Other names for the same wires on the sheet: _1 = in_1; _2 = in_2; _3 = in_3
endmodule

module super_m (
  input  in_1,
  input  in_2,
  input  in_3,
  input  [7:0] in_4,
  input  [7:0] in_5,
  input  [7:0] in_6,
  input  [7:0] in_7,
  input  [7:0] in_8,
  input  [7:0] in_9,
  input  [7:0] in_10,
  input  [7:0] in_11,
  output [7:0] out_12
);

  _8_a_1 u_8_a_1_1 (
    .in_4(in_4[0]), .in_5(in_4[1]), .in_6(in_4[2]), .in_7(in_4[3]), .in_8(in_5[0]), .in_9(in_5[1]),
    .in_10(in_5[2]), .in_11(in_5[3]), .in_12(in_6[0]), .in_13(in_6[1]), .in_14(in_6[2]), .in_15(in_6[3]),
    .in_16(in_7[0]), .in_17(in_7[1]), .in_18(in_7[2]), .in_19(in_7[3]), .in_20(in_8[0]), .in_21(in_8[1]),
    .in_22(in_8[2]), .in_23(in_8[3]), .in_24(in_9[0]), .in_25(in_9[1]), .in_26(in_9[2]), .in_27(in_9[3]),
    .in_28(in_10[0]), .in_29(in_10[1]), .in_30(in_10[2]), .in_31(in_10[3]), .in_32(in_11[0]),
    .in_33(in_11[1]), .in_34(in_11[2]), .in_35(in_11[3]), .in_36(in_4[4]), .in_37(in_4[5]), .in_38(in_4[6]),
    .in_39(in_4[7]), .in_40(in_5[4]), .in_41(in_5[5]), .in_42(in_5[6]), .in_43(in_5[7]), .in_44(in_6[4]),
    .in_45(in_6[5]), .in_46(in_6[6]), .in_47(in_6[7]), .in_48(in_7[4]), .in_49(in_7[5]), .in_50(in_7[6]),
    .in_51(in_7[7]), .in_52(in_8[4]), .in_53(in_8[5]), .in_54(in_8[6]), .in_55(in_8[7]), .in_56(in_9[4]),
    .in_57(in_9[5]), .in_58(in_9[6]), .in_59(in_9[7]), .in_60(in_10[4]), .in_61(in_10[5]), .in_62(in_10[6]),
    .in_63(in_10[7]), .in_64(in_11[4]), .in_65(in_11[5]), .in_66(in_11[6]), .in_67(in_11[7]),
    .out_68(out_12[0]), .out_69(out_12[1]), .out_70(out_12[2]), .out_71(out_12[3]), .out_72(out_12[4]),
    .out_73(out_12[5]), .out_74(out_12[6]), .out_75(out_12[7]), .in_1(in_1), .in_2(in_2), .in_3(in_3));
endmodule

module Finale (
  input  [7:0] in_1,
  input  in_2,
  input  in_3,
  input  in_4,
  input  [7:0] in_5,
  output out_6,
  output [7:0] out_7,
  output out_8
);

  wire [7:0] a_negato_1_out_2, and_8_bit_1_out_3, b_negato_1_out_2, ex_or_8bit_1_out_3, or_8_bit_1_out_3,
       sommatore_8_bit_1_out_4, sottrattore_8_bit_1_out_4;

  sottrattore_8_bit sottrattore_8_bit_1 (.in_1(in_1), .in_2(in_5), .out_3(out_8), .out_4(sottrattore_8_bit_1_out_4));
  Ex_or_8bit ex_or_8bit_1 (.in_1(in_1), .in_2(in_5), .out_3(ex_or_8bit_1_out_3));
  Sommatore_8_bit sommatore_8_bit_1 (.in_1(in_1), .in_2(in_5), .out_3(out_6), .out_4(sommatore_8_bit_1_out_4));
  And_8_bit and_8_bit_1 (.in_1(in_1), .in_2(in_5), .out_3(and_8_bit_1_out_3));
  Or_8_bit or_8_bit_1 (.in_1(in_1), .in_2(in_5), .out_3(or_8_bit_1_out_3));
  A_negato a_negato_1 (.in_1(in_1), .out_2(a_negato_1_out_2));
  super_m super_m_1 (
    .in_4(sommatore_8_bit_1_out_4), .in_5(sottrattore_8_bit_1_out_4), .in_6(and_8_bit_1_out_3),
    .in_7(or_8_bit_1_out_3), .in_8(ex_or_8bit_1_out_3), .in_9(a_negato_1_out_2), .in_10(b_negato_1_out_2),
    .in_11({8{1'b0}}), .in_1(in_3), .in_2(in_4), .in_3(in_2), .out_12(out_7));
  b_negato b_negato_1 (.in_1(in_5), .out_2(b_negato_1_out_2));

  // Other names for the same wires on the sheet: n1[7:0] = in_1; n2[7:0] = in_5
endmodule
